// Logisim project alu.circ as structural Verilog
module Adder (
  input  [31:0] A,
  input  [31:0] B,
  input  AddSub,
  output out_4,
  output [31:0] C
);

  wire and_1_out, and_2_out, not_2_out, not_3_out, not_4_out;
  wire [31:0] multiplexer_1_out, not_1_out;

  Multiplexer #(.width(32)) multiplexer_1 (
    .in0(B), .in1(not_1_out), .out(multiplexer_1_out), .sel(AddSub));  // open: en
  assign not_1_out = ~B;  // NOT_Gate not_1, 32 bits wide
  Adder_part #(.width(32)) adder_1 (.a(A), .b(multiplexer_1_out), .out(C), .cin(AddSub));  // open: cout
  not not_2 (not_2_out, multiplexer_1_out[31]);
  not not_3 (not_3_out, A[31]);
  not not_4 (not_4_out, C[31]);
  and and_1 (and_1_out, A[31], multiplexer_1_out[31], not_4_out);
  and and_2 (and_2_out, not_3_out, not_2_out, C[31]);
  or or_1 (out_4, and_1_out, and_2_out);
endmodule

module Comparator (
  input  [31:0] A,
  input  [31:0] B,
  input  IsUnsigned,
  output [31:0] out_4
);

  wire comparator_1_lt, comparator_2_lt, multiplexer_1_out;

  Comparator_part #(.width(32)) comparator_1 (.a(A), .b(B), .lt(comparator_1_lt));  // open: gt, eq
  Comparator_part #(.width(32), .mode("unsigned")) comparator_2 (.a(A), .b(B), .lt(comparator_2_lt));  // open: gt, eq
  Multiplexer multiplexer_1 (
    .in0(comparator_1_lt), .in1(comparator_2_lt), .out(multiplexer_1_out), .sel(IsUnsigned));  // open: en
  assign out_4 = {{31{1'b0}}, multiplexer_1_out};  // Bit_Extender bit_extender_1
endmodule

module Shift (
  input  [31:0] A,
  input  [31:0] B,
  input  UnsignSign,
  input  LeftRight,
  output [31:0] C
);

  wire and_1_out, and_2_out, l_27or_eeb19545_1_out_2, not_1_out, not_2_out;
  wire [31:0] multiplexer_1_out, multiplexer_2_out, multiplexer_3_out, shifter_1_out, shifter_2_out,
       shifter_3_out;

  L_27Or_eeb19545 l_27or_eeb19545_1 (.in_1(B[31:5]), .out_2(l_27or_eeb19545_1_out_2));
  Shifter #(.width(32), .shift("lr")) shifter_1 (.in(A), .\dist (B[4:0]), .out(shifter_1_out));
  Shifter #(.width(32), .shift("ar")) shifter_2 (.in(A), .\dist (B[4:0]), .out(shifter_2_out));
  Shifter #(.width(32)) shifter_3 (.in(A), .\dist (B[4:0]), .out(shifter_3_out));
  Multiplexer #(.width(32)) multiplexer_1 (
    .in0(shifter_1_out), .in1(shifter_2_out), .out(multiplexer_1_out), .sel(UnsignSign));  // open: en
  Multiplexer #(.width(32)) multiplexer_2 (
    .in0({32{1'b0}}), .in1({32{1'b1}}), .out(multiplexer_2_out), .sel(and_1_out));  // open: en
  and and_1 (and_1_out, A[31], and_2_out);
  Multiplexer #(.width(32)) multiplexer_3 (
    .in0(multiplexer_1_out), .in1(shifter_3_out), .out(multiplexer_3_out), .sel(not_1_out));  // open: en
  not not_1 (not_1_out, LeftRight);
  and and_2 (and_2_out, UnsignSign, LeftRight);
  Multiplexer #(.width(32)) multiplexer_4 (
    .in0(multiplexer_2_out), .in1(multiplexer_3_out), .out(C), .sel(not_2_out));  // open: en
  not not_2 (not_2_out, l_27or_eeb19545_1_out_2);
endmodule

module Multiplier (
  input  [31:0] A,
  input  [31:0] B,
  input  LowerUpper,
  input  SignedUnsigned,
  output [31:0] out_5
);

  wire [31:0] A_0_out_3, adder_1_c, adder_2_c, B_0_out_3, multiplexer_1_out, multiplier_1_cout,
       multiplier_1_out;

  NumOrZero B_0 (.Num(B), .Select(A[31]), .out_3(B_0_out_3));
  NumOrZero A_0 (.Num(A), .Select(B[31]), .out_3(A_0_out_3));
  Multiplier_part #(.width(32)) multiplier_1 (
    .a(A), .b(B), .out(multiplier_1_out), .cout(multiplier_1_cout));  // open: cin
  Adder adder_1 (.A(multiplier_1_cout), .B(A_0_out_3), .AddSub(1'b0), .C(adder_1_c));  // open: out_4
  Adder adder_2 (.A(adder_1_c), .B(B_0_out_3), .AddSub(1'b0), .C(adder_2_c));  // open: out_4
  Multiplexer #(.width(32)) multiplexer_1 (
    .in0(multiplier_1_cout), .in1(adder_2_c), .out(multiplexer_1_out), .sel(SignedUnsigned));  // open: en
  Multiplexer #(.width(32)) multiplexer_2 (
    .in0(multiplier_1_out), .in1(multiplexer_1_out), .out(out_5), .sel(LowerUpper));  // open: en
endmodule

module L_27Or_eeb19545 (
  input  [26:0] in_1,
  output out_2
);

  wire [2:0] or_2_out;
  wire [8:0] or_1_out;

  assign or_1_out = in_1[8:0] | in_1[17:9] | in_1[26:18];  // OR_Gate or_1, 9 bits wide
  assign or_2_out = or_1_out[2:0] | or_1_out[5:3] | or_1_out[8:6];  // OR_Gate or_2, 3 bits wide
  or or_3 (out_2, or_2_out[0], or_2_out[1], or_2_out[2]);
endmodule

module NumOrZero (
  input  [31:0] Num,
  input  Select,
  output [31:0] out_3
);

  Multiplexer #(.width(32)) multiplexer_1 (.in0({32{1'b0}}), .in1(Num), .out(out_3), .sel(Select));  // open: en
endmodule

module BitwiseLogic (
  input  [31:0] A,
  input  [31:0] B,
  input  [1:0] Select,
  output [31:0] out_4
);

  wire [31:0] and_1_out, or_1_out, xor_1_out;

  assign xor_1_out = A ^ B;  // XOR_Gate xor_1, 32 bits wide
  assign or_1_out = A | B;  // OR_Gate or_1, 32 bits wide
  assign and_1_out = A & B;  // AND_Gate and_1, 32 bits wide
  Multiplexer #(.select(2), .width(32)) multiplexer_1 (
    .in0(xor_1_out), .in2(or_1_out), .in3(and_1_out), .out(out_4), .sel(Select));  // open: in1, en
endmodule

module Temp (
);

  main main_1 ();
endmodule

module ALU (
  input  [3:0] ALUSel,
  input  [31:0] A,
  input  [31:0] B,
  output [31:0] Result,
  output OverFlow,
  output Zero
);

  wire [31:0] adder_1_c, bitwiselogic_1_out_4, comparator_1_out_4, multiplier_1_out_5, shift_1_c;

  Adder adder_1 (.A(A), .B(B), .AddSub(ALUSel[2]), .C(adder_1_c), .out_4(OverFlow));
  Comparator comparator_1 (.A(A), .B(B), .out_4(comparator_1_out_4), .IsUnsigned(ALUSel[0]));
  Shift shift_1 (.A(A), .B(B), .UnsignSign(ALUSel[3]), .LeftRight(ALUSel[2]), .C(shift_1_c));
  Multiplier multiplier_1 (
    .A(A), .B(B), .LowerUpper(ALUSel[0]), .SignedUnsigned(ALUSel[1]), .out_5(multiplier_1_out_5));
  BitwiseLogic bitwiselogic_1 (.A(A), .B(B), .Select(ALUSel[1:0]), .out_4(bitwiselogic_1_out_4));
  Multiplexer #(.select(4), .width(32)) multiplexer_1 (
    .in0(adder_1_c), .in1(shift_1_c), .in2(comparator_1_out_4), .in3(comparator_1_out_4),
    .in4(bitwiselogic_1_out_4), .in5(shift_1_c), .in6(bitwiselogic_1_out_4), .in7(bitwiselogic_1_out_4),
    .in8(multiplier_1_out_5), .in9(multiplier_1_out_5), .in11(multiplier_1_out_5), .in12(adder_1_c),
    .in13(shift_1_c), .in15(B), .out(Result), .sel(ALUSel));  // open: in10, in14, en
  Comparator_part #(.width(32)) comparator_2 (.a(Result), .b({32{1'b0}}), .eq(Zero));  // open: gt, lt
endmodule
