// Logisim project processor.circ as structural Verilog
module main (
  output [3:0] ALUOp,
  output [23:0] lineNumber,
  output [31:0] ALUoutput
);

  wire and_1_out, Branch, clk, decode_1_alusrc, RAMwrite, regSrc, reset, write, Zero;
  wire [4:0] rd, rs1, rs2;
  wire [15:0] shifter_2_out;
  wire [23:0] lineNum;
  wire [31:0] adder_1_out, branchRes, Imm, Instr, multiplexer_1_out, multiplexer_2_out, op1, op2, PC,
       RAMread, Reg2Data;
  wire [31:24] shifter_1_out;

  Adder #(.width(32)) adder_1 (.a(32'h4), .b(PC), .out(adder_1_out));  // open: cin, cout
  Button button_1 (.out(reset));
  Clock sysclk ();  // open: out
  Multiplexer #(.width(32)) multiplexer_1 (
    .in0(adder_1_out), .in1(branchRes), .out(multiplexer_1_out), .sel(and_1_out));  // open: en
  and and_1 (and_1_out, Branch, Zero);
  Adder #(.width(24)) adder_2 (.a(lineNum), .b(24'h1), .out(lineNumber));  // open: cin, cout
  Clock clock_1 (.out(clk));
  Register #(.width(32)) register_1 (.D(multiplexer_1_out), .clk(clk), .Q(PC), .clr(reset));  // open: en
  Shifter #(.width(32), .shift("lr")) shifter_1 (.in(PC), .\dist (5'b00010), .out({shifter_1_out, lineNum}));
  ROM #(.addrWidth(24), .dataWidth(32)) rom_1 (.addr(lineNum), .data(Instr));
  Decode decode_1 (
    .Instr(Instr), .ALUSrc(decode_1_alusrc), .Wr(rd), .R1(rs1), .R2(rs2), .write(write), .Imm(Imm),
    .branch(Branch), .RAMwrite(RAMwrite), .regSrc(regSrc), .ALUOp(ALUOp));
  Multiplexer #(.width(32)) multiplexer_2 (
    .in0(ALUoutput), .in1(RAMread), .out(multiplexer_2_out), .sel(regSrc));  // open: en
  register_main main_1 (
    .RegWEn(write), .Clock(clk), .Write_Data(multiplexer_2_out), .Read_Register_1(rs1),
    .Read_Register_2(rs2), .Write_Register(rd), .Reset1(reset), .Read_Data_1(op1), .Read_data_2(Reg2Data));
  ALU alu_1 (.Result(ALUoutput), .Zero(Zero), .ALUSel(ALUOp), .A(op1), .B(op2));  // open: OverFlow
  Multiplexer #(.width(32)) multiplexer_3 (.in0(Imm), .in1(Reg2Data), .out(op2), .sel(decode_1_alusrc));  // open: en
  Adder #(.width(32)) adder_3 (.a(PC), .b(Imm), .out(branchRes));  // open: cin, cout
  Shifter #(.width(16), .shift("lr")) shifter_2 (.in(ALUoutput[15:0]), .\dist (4'b0010), .out(shifter_2_out));
  RAM #(.addrWidth(16), .dataWidth(32), .databus("bibus")) ram_1 (
    .addr(shifter_2_out), .we(RAMwrite), .clk(clk), .din(Reg2Data), .dout(RAMread));  // open: oe

  // Other names for the same wires on the sheet: op[3:0] = ALUOp; res[31:0] = ALUoutput

  // Notes on the sheet:
  //   contents of rom_1 (hex, n*v repeats v):
  //   26100001 26200001 2630000a c6003006 26303fff 66401100 26102000 26204000 c7f0007a 26001000 c6000000
endmodule

module Decode (
  input  [31:0] Instr,
  output [3:0] ALUOp,
  output ALUSrc,
  output [4:0] Wr,
  output [4:0] R1,
  output [4:0] R2,
  output write,
  output [31:0] Imm,
  output branch,
  output RAMwrite,
  output regSrc
);

  wire and_1_out, and_2_out, and_3_out, I_Type, not_2_out, not_3_out, not_4_out, not_5_out, not_6_out,
       not_7_out, or_1_out, or_3_out, R_Type;
  wire [1:0] or_5_out;
  wire [3:0] i_type_decode_1_aluop, r_type_decode_1_alusrc;
  wire [31:0] bit_extender_1_out, bit_extender_2_out, bit_extender_3_out, shifter_1_out;

  or or_1 (or_1_out, I_Type, regSrc, RAMwrite);
  or or_2 (write, R_Type, I_Type, regSrc);
  not not_1 (ALUSrc, or_1_out);
  Instruc_Type instruc_type_1 (
    .opcode(Instr[31:25]), .R_type(R_Type), .I_type(I_Type), .LoadInstruc(regSrc), .StoreInstruc(RAMwrite),
    .BranchInstruc(branch));
  assign bit_extender_1_out = {{20{Instr[23]}}, {Instr[23:20], Instr[6:1], Instr[24], Instr[0]}};  // Bit_Extender bit_extender_1
  I_Type_Decode i_type_decode_1 (.funct3(Instr[19:17]), .funct7(Instr[6:0]), .ALUOp(i_type_decode_1_aluop));
  assign bit_extender_2_out = {{20{Instr[11]}}, Instr[11:0]};  // Bit_Extender bit_extender_2
  assign Imm = or_3_out ? bit_extender_2_out : 32'bz;  // Controlled_Buffer controlled_buffer_1
  or or_3 (or_3_out, I_Type, regSrc);
  assign bit_extender_3_out = {{20{Instr[24]}}, {Instr[24:20], Instr[6:0]}};  // Bit_Extender bit_extender_3
  assign Imm = RAMwrite ? bit_extender_3_out : 32'bz;  // Controlled_Buffer controlled_buffer_2
  Shifter #(.width(32)) shifter_1 (.in(bit_extender_1_out), .\dist (5'b00001), .out(shifter_1_out));
  R_Type_Decode r_type_decode_1 (.funct3(Instr[19:17]), .funct7(Instr[6:0]), .ALUSrc(r_type_decode_1_alusrc));
  Multiplexer #(.select(2), .width(4)) multiplexer_1 (
    .in0(r_type_decode_1_alusrc), .in1(4'b0000), .in2(4'b1100), .in3(i_type_decode_1_aluop), .out(ALUOp),
    .sel(or_5_out));  // open: en
  or or_4 (or_5_out[1], and_1_out, I_Type);
  and and_1 (and_1_out, not_3_out, not_2_out, branch);
  not not_2 (not_2_out, RAMwrite);
  not not_3 (not_3_out, regSrc);
  assign Imm = branch ? shifter_1_out : 32'bz;  // Controlled_Buffer controlled_buffer_3
  and and_2 (and_2_out, regSrc, not_4_out, not_5_out);
  not not_4 (not_4_out, RAMwrite);
  not not_5 (not_5_out, branch);
  or or_5 (or_5_out[0], and_2_out, I_Type, and_3_out);
  and and_3 (and_3_out, not_6_out, RAMwrite, not_7_out);
  not not_6 (not_6_out, regSrc);
  not not_7 (not_7_out, branch);

  assign R1 = Instr[16:12];
  assign R2 = Instr[11:7];
  assign Wr = Instr[24:20];

  // Other names for the same wires on the sheet: Branch_Type = branch; I_Type_Immediate[11:0] = Instr[11:0];
  //   rs2[4:0] = Instr[11:7]; rs1[4:0] = Instr[16:12]; funct3[2:0] = Instr[19:17]; opcode[6:0] = Instr[31:25];
  //   Load_Type = regSrc; B_Type_Immediate[11:0] = {Instr[23:20], Instr[6:1], Instr[24], Instr[0]};
  //   funct7[6:0] = Instr[6:0]; immUpper[6:0] = Instr[6:0]; S_Type_Immediate[11:0] = {Instr[24:20], Instr[6:0]};
  //   rd[4:0] = Instr[24:20]; Store_Type = RAMwrite
endmodule

module R_Type_Decode (
  input  [2:0] funct3,
  input  [6:0] funct7,
  output [3:0] ALUSrc
);

  wire not_1_out, or_1_out;

  not not_1 (not_1_out, or_1_out);
  or or_1 (or_1_out, funct3[0], funct3[1], funct3[2]);
  Multiplexer #(.width(4)) multiplexer_1 (
    .in0({1'b0, funct3}), .in1({{2{funct7[5]}}, funct7[1:0]}), .out(ALUSrc), .sel(not_1_out));  // open: en
endmodule

module Instruc_Type (
  input  [6:0] opcode,
  output R_type,
  output I_type,
  output LoadInstruc,
  output StoreInstruc,
  output BranchInstruc
);

  Comparator #(.width(7)) comparator_1 (.a(opcode), .b(7'b0110011), .eq(R_type));  // open: gt, lt
  Comparator #(.width(7)) comparator_2 (.a(opcode), .b(7'b0010011), .eq(I_type));  // open: gt, lt
  Comparator #(.width(7)) comparator_3 (.a(opcode), .b(7'b0000011), .eq(LoadInstruc));  // open: gt, lt
  Comparator #(.width(7)) comparator_4 (.a(opcode), .b(7'b0100011), .eq(StoreInstruc));  // open: gt, lt
  Comparator #(.width(7)) comparator_5 (.a(opcode), .b(7'b1100011), .eq(BranchInstruc));  // open: gt, lt
endmodule

module I_Type_Decode (
  input  [2:0] funct3,
  input  [6:0] funct7,
  output [3:0] ALUOp
);


  assign ALUOp = {1'b0, funct3};
endmodule
