// Logisim project register.circ as structural Verilog: 2 circuits, main circuit main
module main (
  input  RegWEn,
  input  Clock,
  input  [31:0] Write_Data,
  input  [4:0] Read_Register_1,
  input  [4:0] Read_Register_2,
  input  [4:0] Write_Register,
  input  Reset1,
  output [31:0] Read_Data_1,
  output [31:0] Read_data_2
);

  wire and_1_out, and_2_out, and_3_out, and_4_out, and_5_out, and_6_out, and_7_out, and_8_out, and_9_out,
       and_10_out, and_11_out, and_12_out, and_13_out, and_14_out, and_15_out, and_16_out, decoder_1_out0,
       decoder_1_out1, decoder_1_out2, decoder_1_out3, decoder_2_out0, decoder_2_out1, decoder_2_out2,
       decoder_2_out3;
  wire [31:0] multiplexer_1_out, multiplexer_2_out, multiplexer_4_out, multiplexer_5_out, multiplexer_6_out,
       multiplexer_7_out, multiplexer_8_out, multiplexer_10_out, r0, r1, r2, r3, r4, r5, r6, r7, r8, r9, r10,
       r11, r12, r13, r14, r15;

  Decoder #(.select(2)) decoder_1 (
    .out0(decoder_1_out0), .out1(decoder_1_out1), .out2(decoder_1_out2), .out3(decoder_1_out3),
    .sel(Write_Register[1:0]));  // open: en
  Register #(.width(32)) register_1 (.D(Write_Data), .en(and_1_out), .clk(Clock), .Q(r2), .clr(Reset1));
  and and_1 (and_1_out, decoder_1_out2, RegWEn, decoder_2_out0);
  Register #(.width(32)) register_2 (.D(Write_Data), .en(and_2_out), .clk(Clock), .Q(r0), .clr(Reset1));
  and and_2 (and_2_out, decoder_1_out0, 1'b0, decoder_2_out0);
  Register #(.width(32)) register_3 (.D(Write_Data), .en(and_3_out), .clk(Clock), .Q(r1), .clr(Reset1));
  and and_3 (and_3_out, decoder_1_out1, RegWEn, decoder_2_out0);
  Register #(.width(32)) register_4 (.D(Write_Data), .en(and_4_out), .clk(Clock), .Q(r3), .clr(Reset1));
  and and_4 (and_4_out, decoder_1_out3, RegWEn, decoder_2_out0);
  Decoder #(.select(2)) decoder_2 (
    .out0(decoder_2_out0), .out1(decoder_2_out1), .out2(decoder_2_out2), .out3(decoder_2_out3),
    .sel(Write_Register[3:2]));  // open: en
  Register #(.width(32)) register_5 (.D(Write_Data), .en(and_5_out), .clk(Clock), .Q(r4), .clr(Reset1));
  and and_5 (and_5_out, decoder_1_out0, RegWEn, decoder_2_out1);
  Register #(.width(32)) register_6 (.D(Write_Data), .en(and_6_out), .clk(Clock), .Q(r5), .clr(Reset1));
  and and_6 (and_6_out, decoder_1_out1, RegWEn, decoder_2_out1);
  Register #(.width(32)) register_7 (.D(Write_Data), .en(and_7_out), .clk(Clock), .Q(r6), .clr(Reset1));
  and and_7 (and_7_out, decoder_1_out2, RegWEn, decoder_2_out1);
  Register #(.width(32)) register_8 (.D(Write_Data), .en(and_8_out), .clk(Clock), .Q(r7), .clr(Reset1));
  and and_8 (and_8_out, decoder_1_out3, RegWEn, decoder_2_out1);
  Register #(.width(32)) register_9 (.D(Write_Data), .en(and_9_out), .clk(Clock), .Q(r8), .clr(Reset1));
  and and_9 (and_9_out, decoder_1_out0, RegWEn, decoder_2_out2);
  Register #(.width(32)) register_10 (.D(Write_Data), .en(and_10_out), .clk(Clock), .Q(r9), .clr(Reset1));
  and and_10 (and_10_out, decoder_1_out1, RegWEn, decoder_2_out2);
  Register #(.width(32)) register_11 (.D(Write_Data), .en(and_11_out), .clk(Clock), .Q(r10), .clr(Reset1));
  and and_11 (and_11_out, decoder_1_out2, RegWEn, decoder_2_out2);
  Register #(.width(32)) register_12 (.D(Write_Data), .en(and_12_out), .clk(Clock), .Q(r11), .clr(Reset1));
  and and_12 (and_12_out, decoder_1_out3, RegWEn, decoder_2_out2);
  Register #(.width(32)) register_13 (.D(Write_Data), .en(and_13_out), .clk(Clock), .Q(r12), .clr(Reset1));
  and and_13 (and_13_out, decoder_1_out0, RegWEn, decoder_2_out3);
  Register #(.width(32)) register_14 (.D(Write_Data), .en(and_14_out), .clk(Clock), .Q(r13), .clr(Reset1));
  and and_14 (and_14_out, decoder_1_out1, RegWEn, decoder_2_out3);
  Register #(.width(32)) register_15 (.D(Write_Data), .en(and_15_out), .clk(Clock), .Q(r14), .clr(Reset1));
  and and_15 (and_15_out, decoder_1_out2, RegWEn, decoder_2_out3);
  Register #(.width(32)) register_16 (.D(Write_Data), .en(and_16_out), .clk(Clock), .Q(r15), .clr(Reset1));
  and and_16 (and_16_out, decoder_1_out3, RegWEn, decoder_2_out3);
  Multiplexer #(.select(2), .width(32), .enable("false")) multiplexer_1 (
    .in0(r0), .in1(r1), .in2(r2), .in3(r3), .out(multiplexer_1_out), .sel(Read_Register_1[1:0]));
  Multiplexer #(.select(2), .width(32), .enable("false")) multiplexer_2 (
    .in0(r4), .in1(r5), .in2(r6), .in3(r7), .out(multiplexer_2_out), .sel(Read_Register_1[1:0]));
  Multiplexer #(.select(2), .width(32), .enable("false")) multiplexer_3 (
    .in0(multiplexer_1_out), .in1(multiplexer_2_out), .in2(multiplexer_4_out), .in3(multiplexer_5_out),
    .out(Read_Data_1), .sel(Read_Register_1[3:2]));
  Multiplexer #(.select(2), .width(32), .enable("false")) multiplexer_4 (
    .in0(r8), .in1(r9), .in2(r10), .in3(r11), .out(multiplexer_4_out), .sel(Read_Register_1[1:0]));
  Multiplexer #(.select(2), .width(32), .enable("false")) multiplexer_5 (
    .in0(r12), .in1(r13), .in2(r14), .in3(r15), .out(multiplexer_5_out), .sel(Read_Register_1[1:0]));
  Multiplexer #(.select(2), .width(32), .enable("false")) multiplexer_6 (
    .in0(r0), .in1(r1), .in2(r2), .in3(r3), .out(multiplexer_6_out), .sel(Read_Register_2[1:0]));
  Multiplexer #(.select(2), .width(32), .enable("false")) multiplexer_7 (
    .in0(r4), .in1(r5), .in2(r6), .in3(r7), .out(multiplexer_7_out), .sel(Read_Register_2[1:0]));
  Multiplexer #(.select(2), .width(32), .enable("false")) multiplexer_8 (
    .in0(r8), .in1(r9), .in2(r10), .in3(r11), .out(multiplexer_8_out), .sel(Read_Register_2[1:0]));
  Multiplexer #(.select(2), .width(32), .enable("false")) multiplexer_9 (
    .in0(multiplexer_6_out), .in1(multiplexer_7_out), .in2(multiplexer_8_out), .in3(multiplexer_10_out),
    .out(Read_data_2), .sel(Read_Register_2[3:2]));
  Multiplexer #(.select(2), .width(32), .enable("false")) multiplexer_10 (
    .in0(r12), .in1(r13), .in2(r14), .in3(r15), .out(multiplexer_10_out), .sel(Read_Register_2[1:0]));

  // Other names for the same wires on the sheet: r = Reset1
endmodule

module test (
);

  main main_1 ();  // open: RegWEn, Clock, Write_Data, Read_Register_1, Read_Register_2, Write_Register, Reset1, Read_Data_1, Read_data_2
endmodule
